// Digital circuit Half7474.dig as structural Verilog
module Half7474 (
  input  nSD,
  input  D,
  input  CP,
  input  nRD,
  output Q,
  output nQ
);

  wire and_1_out, d_ff_as_1_nq;

  D_FF_AS d_ff_as_1 (.Set(~nSD), .D(D), .C(CP), .Clr(~nRD), .Q(Q), .nQ(d_ff_as_1_nq));
  and and_1 (and_1_out, ~nSD, ~nRD);  // And
  or or_1 (nQ, d_ff_as_1_nq, and_1_out);

  // Notes on the sheet:
  //   Q: pin 5
  //   nQ: pin 6
  //   nSD: pin 4
  //   D: pin 2
  //   CP: pin 3
  //   nRD: pin 1
endmodule
