// Digital circuit ProgramCounter.dig as structural Verilog
module ProgramCounter (
  input  [23:0] P,
  input  CK,
  input  nLD,
  input  nOE,
  input  RESET,
  input  BFLASH,
  output [23:0] Q,
  output Neg,
  output [23:0] Spy
);

  wire _74ls157_1_y1, _74ls157_1_y2, _74ls157_1_y3, _74ls157_1_y4, _74ls157_2_y1, _74ls157_2_y2,
       _74ls157_2_y3, _74ls157_2_y4, _74ls157_3_y1, _74ls157_3_y2, _74ls157_3_y3, _74ls157_3_y4,
       _74ls157_4_y1, _74ls157_4_y2, _74ls157_4_y3, _74ls157_4_y4, _74ls157_5_y1, _74ls157_5_y2,
       _74ls157_5_y3, _74ls157_5_y4, _74ls157_6_y1, _74ls157_6_y2, _74ls157_6_y3, _74ls157_6_y4,
       _74ls163_1_tc, _74ls163_2_tc, _74ls163_3_tc, _74ls163_4_tc, _74ls163_5_tc, _74ls163_6_tc;

  _74LS157 _74ls157_1 (
    .S(RESET), .A1(P[0]), .A2(P[1]), .A3(P[2]), .A4(P[3]), .B1(1'b0), .B2(1'b0), .B3(1'b0), .B4(1'b0),
    .G(1'b0), .Y1(_74ls157_1_y1), .Y2(_74ls157_1_y2), .Y3(_74ls157_1_y3), .Y4(_74ls157_1_y4));
  _74LS157 _74ls157_2 (
    .S(RESET), .A1(P[4]), .A2(P[5]), .A3(P[6]), .A4(P[7]), .B1(1'b0), .B2(1'b0), .B3(1'b0), .B4(1'b0),
    .G(1'b0), .Y1(_74ls157_2_y1), .Y2(_74ls157_2_y2), .Y3(_74ls157_2_y3), .Y4(_74ls157_2_y4));
  _74LS157 _74ls157_3 (
    .S(RESET), .A1(P[8]), .A2(P[9]), .A3(P[10]), .A4(P[11]), .B1(1'b0), .B2(1'b0), .B3(1'b0), .B4(1'b0),
    .G(1'b0), .Y1(_74ls157_3_y1), .Y2(_74ls157_3_y2), .Y3(_74ls157_3_y3), .Y4(_74ls157_3_y4));
  _74LS157 _74ls157_4 (
    .S(RESET), .A1(P[12]), .A2(P[13]), .A3(P[14]), .A4(P[15]), .B1(1'b0), .B2(1'b0), .B3(1'b0), .B4(1'b0),
    .G(1'b0), .Y1(_74ls157_4_y1), .Y2(_74ls157_4_y2), .Y3(_74ls157_4_y3), .Y4(_74ls157_4_y4));
  _74LS157 _74ls157_5 (
    .S(RESET), .A1(P[16]), .A2(P[17]), .A3(P[18]), .A4(P[19]), .B1(1'b0), .B2(1'b0), .B3(1'b0), .B4(1'b0),
    .G(1'b0), .Y1(_74ls157_5_y1), .Y2(_74ls157_5_y2), .Y3(_74ls157_5_y3), .Y4(_74ls157_5_y4));
  _74LS157 _74ls157_6 (
    .S(RESET), .A1(P[20]), .A2(P[21]), .A3(P[22]), .A4(P[23]), .B1(1'b0), .B2(BFLASH), .B3(BFLASH),
    .B4(1'b0), .G(1'b0), .Y1(_74ls157_6_y1), .Y2(_74ls157_6_y2), .Y3(_74ls157_6_y3), .Y4(_74ls157_6_y4));
  _74LS163 _74ls163_1 (
    .nPE(nLD), .nSR(1'b1), .CP(CK), .CET(1'b1), .CEP(1'b1), .P0(_74ls157_1_y1), .P1(_74ls157_1_y2),
    .P2(_74ls157_1_y3), .P3(_74ls157_1_y4), .TC(_74ls163_1_tc), .Q0(Spy[0]), .Q1(Spy[1]), .Q2(Spy[2]),
    .Q3(Spy[3]));
  _74LS163 _74ls163_2 (
    .nPE(nLD), .nSR(1'b1), .CP(CK), .CET(_74ls163_1_tc), .CEP(1'b1), .P0(_74ls157_2_y1), .P1(_74ls157_2_y2),
    .P2(_74ls157_2_y3), .P3(_74ls157_2_y4), .TC(_74ls163_2_tc), .Q0(Spy[4]), .Q1(Spy[5]), .Q2(Spy[6]),
    .Q3(Spy[7]));
  _74LS163 _74ls163_3 (
    .nPE(nLD), .nSR(1'b1), .CP(CK), .CET(_74ls163_2_tc), .CEP(1'b1), .P0(_74ls157_3_y1), .P1(_74ls157_3_y2),
    .P2(_74ls157_3_y3), .P3(_74ls157_3_y4), .TC(_74ls163_3_tc), .Q0(Spy[8]), .Q1(Spy[9]), .Q2(Spy[10]),
    .Q3(Spy[11]));
  _74LS163 _74ls163_4 (
    .nPE(nLD), .nSR(1'b1), .CP(CK), .CET(_74ls163_3_tc), .CEP(1'b1), .P0(_74ls157_4_y1), .P1(_74ls157_4_y2),
    .P2(_74ls157_4_y3), .P3(_74ls157_4_y4), .TC(_74ls163_4_tc), .Q0(Spy[12]), .Q1(Spy[13]), .Q2(Spy[14]),
    .Q3(Spy[15]));
  _74LS163 _74ls163_5 (
    .nPE(nLD), .nSR(1'b1), .CP(CK), .CET(_74ls163_4_tc), .CEP(1'b1), .P0(_74ls157_5_y1), .P1(_74ls157_5_y2),
    .P2(_74ls157_5_y3), .P3(_74ls157_5_y4), .TC(_74ls163_5_tc), .Q0(Spy[16]), .Q1(Spy[17]), .Q2(Spy[18]),
    .Q3(Spy[19]));
  _74LS163 _74ls163_6 (
    .nPE(nLD), .nSR(1'b1), .CP(CK), .CET(_74ls163_5_tc), .CEP(1'b1), .P0(_74ls157_6_y1), .P1(_74ls157_6_y2),
    .P2(_74ls157_6_y3), .P3(_74ls157_6_y4), .TC(_74ls163_6_tc), .Q0(Spy[20]), .Q1(Spy[21]), .Q2(Spy[22]),
    .Q3(Neg));
  // _74LS245 _74ls245_1: pin names not known; wires that end beside it: 1'b1, nOE
  // _74LS245 _74ls245_2: pin names not known; wires that end beside it: 1'b1, nOE
  // _74LS245 _74ls245_3: pin names not known; wires that end beside it: 1'b1, nOE

  assign Spy[23] = Neg;

  // Notes on the sheet:
  //   P: default 1
  //   nLD: default 1
  //   nOE: default 1
endmodule
