// Digital circuit SUBLEQ24.dig as structural Verilog
module SUBLEQ24 (
  input  clk,
  input  XTAL,
  input  TraceClock,
  input  TRACE,
  input  HALT,
  input  [7:0] GPIO2in,
  input  in_7,
  input  in_8,
  input  in_9,
  input  in_10,
  input  in_11,
  input  in_12,
  input  in_13,
  input  in_14,
  input  in_15,
  input  in_16,
  input  in_17,
  input  in_18,
  input  in_19
);

  wire _74ls138_1_ny0, _74ls138_1_ny1, _74ls138_1_ny2, _74ls138_1_ny3, _74ls138_1_ny4, _74ls138_1_ny5,
       _74ls138_1_ny6, _74ls138_1_ny7, _74ls157_1_y1, _74ls157_1_y2, _74ls157_1_y3, _74ls157_1_y4,
       _74ls157_2_y1, _74ls157_2_y2, _74ls157_2_y3, _74ls157_2_y4, _74ls157_3_y1, _74ls157_3_y2,
       _74ls157_3_y3, _74ls157_3_y4, _74ls157_4_y1, _74ls157_4_y2, _74ls157_4_y3, _74ls157_4_y4,
       _74ls157_5_y1, _74ls157_5_y2, _74ls157_5_y3, _74ls157_5_y4, _74ls157_6_y1, _74ls157_6_y2,
       _74ls157_6_y3, _74ls157_6_y4, _74ls163_1_q0, _74ls163_1_q1, _74ls163_1_q2, _74ls163_2_tc,
       _74ls163_3_tc, _74ls163_4_tc, _74ls163_5_tc, _74ls163_6_tc, _74ls163_7_tc, _74ls165_1_qh,
       _74ls165_2_nqh, _74ls238_1_y0, _74ls238_1_y1, _74ls238_1_y2, _74ls238_1_y3, _74ls238_1_y4,
       _74ls238_1_y5, _74ls238_1_y6, _74ls238_1_y7, _74ls238_2_y0, _74ls238_2_y1, _74ls238_2_y2,
       _74ls238_2_y3, _74ls238_2_y4, _74ls238_2_y5, _74ls238_2_y6, _74ls238_2_y7, _74ls283_1_p2,
       _74ls283_2_p2, _74ls283_3_p2, _74ls283_4_p2, _74ls283_5_p2, _74ls393_1__1qd, _74ls393_1__2qa,
       _74ls393_1__2qd, _74ls393_2__1qd, _74ls393_2__2qc, _74ls393_2__2qd, AisNeg, and_1_out, and_2_out,
       and_3_out, and_4_out, and_5_out, and_6_out, and_27_out, and_28_out, and_29_out, and_30_out, BisNeg,
       delay_1_out, delay_2_out, delay_4_out, half7474_3_q, half7474_4_q, half7474_5_q, half7474_6_nq,
       half7474_7_nq, half7474_8_nq, half7474_9_q, half7474_10_nq, half7474_11_nq, half7474_12_q,
       half7474_13_nq, half7474_13_q, half7474_14_q, half7474_15_q, half7474_18_q, half7474_19_q,
       half7474_20_q, half7474_21_nq, half7474_22_q, HALT_t, IOread, IOreadP, IOrw, IOwrite, IOwriteP, isLEQ,
       M_out, nand_1_out, nand_2_out, nand_3_out, nand_4_out, nand_6_out, nand_7_out, nand_10_out,
       nand_11_out, nand_12_out, nand_13_out, nand_14_out, nCK, nE_PC, nIOread, nIOwrite, nMAR_E, noIO,
       nor_1_out, nor_2_out, nor_3_out, nor_4_out, nor_5_out, nor_6_out, nor_7_out, nor_8_out, not_1_out,
       not_2_out, not_4_out, not_9_out, not_10_out, not_11_out, not_12_out, not_13_out, not_21_out,
       not_22_out, not_23_out, not_24_out, not_25_out, not_27_out, not_28_out, not_29_out, not_30_out,
       not_31_out, not_32_out, nPC_LD, nPOR, nRD, nReset, nResetP, nResult_E, nUARTbusy, nWR, or_1_out,
       or_2_out, or_3_out, or_4_out, or_5_out, or_6_out, or_9_out, or_10_out, or_11_out, or_12_out,
       or_13_out, or_14_out, PC_FLASH, POR, R_out, reset_1_out, reset_2_out, S_out, Tick, TS0, TS1, TS2, TS3,
       TS3io, TS3ior, TS3iow, TS3noio, TS4, TS4io, TS4ior, TS4iow, TS4noio, TS5, TS5io, TS5ior, TS5iow,
       TS5noio, TS6, TS6io, TS6ior, TS6iow, TS6noio, TS7, TS7io, TS7ior, TS7iow, TS7noio,
       uart_telnet_gw_1_tx, UARTBusy, UARTdrives, xor_1_out, Z_out;
  wire [3:0] pulldown_2_out_2, pulldown_2_out_3, pulldown_3_out, pulldown_3_out_2, SpyIOa;
  wire [7:0] _74ls574_8_q0, not_26_out;
  wire [22:0] SPY_PC;
  wire [23:0] ABUS, d_ff_1_q, DBUS, not_7_out, not_8_out, ramasync_1_q, SPY_sub;
  wire [23:8] pulldown_2_out, pulldown_3_out_3;

  Button F (.out(PC_FLASH));
  Button Z (.out(Z_out));
  Button M (.out(M_out));
  Button R (.out(R_out));
  Button S (.out(S_out));
  or or_1 (or_1_out, nWR, POR);
  not not_1 (not_1_out, TS0);
  or or_2 (or_2_out, PC_FLASH, POR, Z_out);
  and and_1 (and_1_out, TRACE, TraceClock);
  // Probe on ABUS
  not not_2 (not_2_out, TS0);
  or or_3 (or_3_out, R_out, S_out, and_1_out);
  RAMAsync #(.AddrBits(24), .Bits(24), .isProgramMemory("true")) ramasync_1 (
    .A(ABUS), .D(DBUS), .we(~or_1_out), .Q(ramasync_1_q));
  or or_4 (or_4_out, ~or_1_out, nRD);  // Or
  // _74LS574 _74ls574_1: pin names not known; wires that end beside it: nMAR_E, in_7
  // _74LS574 _74ls574_2: pin names not known; wires that end beside it: nMAR_E, in_7
  // _74LS574 _74ls574_3: pin names not known; wires that end beside it: nMAR_E, in_7
  Half7474 half7474_1 (.nSD(1'b1), .D(DBUS[23]), .CP(in_8), .nRD(not_1_out), .Q(AisNeg));  // open: nQ
  Half7474 half7474_2 (.nSD(1'b1), .D(DBUS[23]), .CP(in_9), .nRD(not_2_out), .Q(BisNeg));  // open: nQ
  not not_3 (nReset, or_2_out);
  Half7474 half7474_3 (.nSD(1'b1), .D(HALT), .CP(XTAL), .nRD(nResetP), .Q(half7474_3_q));  // open: nQ
  Half7474 half7474_4 (.nSD(1'b1), .D(R_out), .CP(XTAL), .nRD(nResetP), .Q(half7474_4_q));  // open: nQ
  Half7474 half7474_5 (.nSD(1'b1), .D(or_3_out), .CP(XTAL), .nRD(nResetP), .Q(half7474_5_q));  // open: nQ
  RS_FF_AS rs_ff_as_1 (.S(TraceClock), .R(1'b0), .Q(nPOR), .nQ(POR));
  PullUp #(.Bits(24)) pullup_1 ();  // open: out
  // Probe on DBUS
  assign DBUS = ~or_4_out ? ramasync_1_q : 24'bz;  // DriverInvSel driverinvsel_1
  PullDown #(.Bits(24)) pulldown_1 (.out(DBUS));
  Half7474 half7474_6 (.nSD(1'b1), .D(half7474_3_q), .CP(XTAL), .nRD(nResetP), .nQ(half7474_6_nq));  // open: Q
  Half7474 half7474_7 (.nSD(1'b1), .D(half7474_4_q), .CP(XTAL), .nRD(nResetP), .nQ(half7474_7_nq));  // open: Q
  Half7474 half7474_8 (.nSD(1'b1), .D(half7474_5_q), .CP(XTAL), .nRD(nResetP), .nQ(half7474_8_nq));  // open: Q
  Half7474 half7474_9 (.nSD(1'b1), .D(or_2_out), .CP(XTAL), .nRD(1'b1), .Q(half7474_9_q));  // open: nQ
  and and_2 (and_2_out, half7474_3_q, half7474_6_nq);
  and and_3 (and_3_out, half7474_4_q, half7474_7_nq);
  and and_4 (and_4_out, half7474_5_q, half7474_8_nq);
  or or_5 (or_5_out, and_2_out, and_3_out);
  not not_4 (not_4_out, and_4_out);
  Half7474 half7474_10 (.nSD(nResetP), .D(in_19), .CP(XTAL), .nRD(1'b1), .nQ(half7474_10_nq));  // open: Q
  // Probe on in_7
  Half7474 half7474_11 (.nSD(1'b1), .D(half7474_9_q), .CP(XTAL), .nRD(1'b1), .nQ(half7474_11_nq));  // open: Q
  Half7474 half7474_12 (.nSD(not_4_out), .D(1'b0), .CP(1'b0), .nRD(half7474_10_nq), .Q(half7474_12_q));  // open: nQ
  // _74LS564 _74ls564_1: pin names not known; wires that end beside it: 1'b0, in_16
  // _74LS564 _74ls564_2: pin names not known; wires that end beside it: 1'b0, in_16
  // _74LS564 _74ls564_3: pin names not known; wires that end beside it: 1'b0, in_16
  // _74LS574 _74ls574_4: pin names not known; wires that end beside it: 1'b0, in_17
  // _74LS574 _74ls574_5: pin names not known; wires that end beside it: 1'b0, in_17
  // _74LS574 _74ls574_6: pin names not known; wires that end beside it: 1'b0, in_17
  and and_5 (and_5_out, half7474_9_q, half7474_11_nq);
  Half7474 half7474_13 (
    .nSD(1'b1), .D(half7474_13_nq), .CP(or_5_out), .nRD(nResetP), .Q(half7474_13_q), .nQ(half7474_13_nq));
  // Probe PROGRAM COUNTER on {HALT_t, SPY_PC}
  // Probe LATCHED IO ADDRESS on SpyIOa
  // Probe SUBTRACTOR on SPY_sub
  D_FF #(.Bits(24)) d_ff_1 (.D(DBUS), .C(in_7), .Q(d_ff_1_q));  // open: nQ
  not not_5 (nResetP, and_5_out);
  // Probe on half7474_13_q
  or or_6 (or_6_out, half7474_13_q, half7474_12_q);
  // Probe on half7474_12_q
  // Probe MAR on d_ff_1_q
  Half7474 half7474_14 (.nSD(1'b1), .D(M_out), .CP(nCK), .nRD(nResetP), .Q(half7474_14_q));  // open: nQ
  Half7474 half7474_15 (.nSD(1'b1), .D(or_6_out), .CP(nCK), .nRD(nResetP), .Q(half7474_15_q));  // open: nQ
  PullDown #(.Bits(24)) pulldown_2 (.out({pulldown_2_out, pulldown_2_out_3, pulldown_2_out_2}));
  PullDown #(.Bits(24)) pulldown_3 (.out({pulldown_3_out_3, pulldown_3_out_2, pulldown_3_out}));
  LED RUN (.in(half7474_15_q));
  not not_6 (nCK, XTAL);
  and and_6 (and_6_out, half7474_15_q, XTAL);
  assign not_7_out = ~SPY_sub;  // Not not_7, 24 bits wide
  assign not_8_out = ~{pulldown_2_out, pulldown_2_out_3, pulldown_2_out_2};  // Not not_8, 24 bits wide
  or or_7 (Tick, and_5_out, half7474_14_q, and_6_out);
  // Probe on and_6_out
  // Probe ~SUBTRACTOR on not_7_out
  // Probe ~AVAL on not_8_out
  // Probe BVAL on {pulldown_3_out_3, pulldown_3_out_2, pulldown_3_out}
  // _74LS283 _74ls283_1: pin names not known; wires that end beside it: nIOwrite, _74ls283_1_p2
  _74LS163 _74ls163_1 (
    .nPE(nReset), .nSR(1'b1), .CP(Tick), .CET(1'b1), .CEP(1'b1), .P0(1'b0), .P1(1'b0), .P2(1'b0), .P3(1'b0),
    .Q0(_74ls163_1_q0), .Q1(_74ls163_1_q1), .Q2(_74ls163_1_q2));  // open: TC, Q3
  // Probe on Tick
  // _74LS283 _74ls283_2: pin names not known; wires that end beside it: _74ls283_1_p2, _74ls283_2_p2
  nor nor_1 (nor_1_out, SPY_sub[2], SPY_sub[1], SPY_sub[0]);
  nor nor_2 (nor_2_out, SPY_sub[5], SPY_sub[4], SPY_sub[3]);
  // Probe on _74ls163_1_q2
  nor nor_3 (nor_3_out, SPY_sub[8], SPY_sub[7], SPY_sub[6]);
  nor nor_4 (nor_4_out, SPY_sub[11], SPY_sub[10], SPY_sub[9]);
  Delay #(.delayTime(10)) delay_1 (.in(not_9_out), .out(delay_1_out));
  not not_9 (not_9_out, Tick);
  not not_10 (not_10_out, nReset);
  Delay #(.delayTime(10)) delay_2 (.in(not_10_out), .out(delay_2_out));
  and and_7 (TS3ior, TS3, IOread);
  and and_8 (TS4ior, TS4, IOread);
  and and_9 (TS5ior, TS5, IOread);
  and and_10 (TS6ior, TS6, IOread);
  and and_11 (TS7ior, TS7, IOread);
  nand nand_1 (nand_1_out, TS3, BisNeg);
  not not_11 (not_11_out, TS0);
  nand nand_2 (nand_2_out, TS1, AisNeg);
  not not_12 (not_12_out, TS0);
  LED led_1 (.in(TS0));
  // _74LS283 _74ls283_3: pin names not known; wires that end beside it: _74ls283_2_p2, _74ls283_3_p2
  nor nor_5 (nor_5_out, SPY_sub[14], SPY_sub[13], SPY_sub[12]);
  nor nor_6 (nor_6_out, SPY_sub[17], SPY_sub[16], SPY_sub[15]);
  nand nand_3 (nand_3_out, nor_8_out, nor_7_out, nor_6_out, nor_5_out, nor_4_out, nor_3_out, nor_2_out, nor_1_out);
  xor xor_1 (xor_1_out, delay_1_out, delay_2_out);
  LED led_2 (.in(TS1));
  nor nor_7 (nor_7_out, SPY_sub[20], SPY_sub[19], SPY_sub[18]);
  _74LS238 _74ls238_1 (
    .A(_74ls163_1_q0), .B(_74ls163_1_q1), .C(_74ls163_1_q2), .G(nReset), .nGA(1'b0), .nGB(1'b0),
    .Y0(_74ls238_1_y0), .Y1(_74ls238_1_y1), .Y2(_74ls238_1_y2), .Y3(_74ls238_1_y3), .Y4(_74ls238_1_y4),
    .Y5(_74ls238_1_y5), .Y6(_74ls238_1_y6), .Y7(_74ls238_1_y7));
  Half7474 half7474_16 (.nSD(nand_1_out), .D(1'b0), .CP(nResetP), .nRD(not_11_out), .Q(IOwrite), .nQ(nIOwrite));
  Half7474 half7474_17 (.nSD(nand_2_out), .D(1'b0), .CP(nResetP), .nRD(not_12_out), .Q(IOread), .nQ(nIOread));
  LED led_3 (.in(TS2));
  // _74LS283 _74ls283_4: pin names not known; wires that end beside it: _74ls283_3_p2, _74ls283_4_p2
  nor nor_8 (nor_8_out, SPY_sub[23], SPY_sub[22], SPY_sub[21]);
  Reset #(.invertOutput("false")) reset_1 (.out(reset_1_out));
  and and_12 (TS3iow, TS3, IOwrite);
  and and_13 (TS4iow, TS4, IOwrite);
  and and_14 (TS5iow, TS5, IOwrite);
  and and_15 (TS6iow, TS6, IOwrite);
  and and_16 (TS7iow, TS7, IOwrite);
  LightBulb lightbulb_1 (.A(IOwrite), .B(1'b0));
  LightBulb lightbulb_2 (.A(IOread), .B(1'b0));
  LED led_4 (.in(TS3));
  LED led_5 (.in(TS4));
  LED led_6 (.in(TS3noio));
  LED led_7 (.in(TS4noio));
  LED led_8 (.in(TS3io));
  LED led_9 (.in(TS4io));
  LED led_10 (.in(TS3ior));
  LED led_11 (.in(TS4ior));
  LED led_12 (.in(TS3iow));
  LED led_13 (.in(TS4iow));
  _74LS574 _74ls574_7 (
    .nOC(reset_1_out), .CLK(xor_1_out), .D0(_74ls238_1_y0), .D1(_74ls238_1_y1), .D2(_74ls238_1_y2),
    .D3(_74ls238_1_y3), .D4(_74ls238_1_y4), .D5(_74ls238_1_y5), .D6(_74ls238_1_y6), .D7(_74ls238_1_y7),
    .Q0(TS0), .Q1(TS1), .Q2(TS2), .Q3(TS3), .Q4(TS4), .Q5(TS5), .Q6(TS6), .Q7(TS7));  // open: SPY
  // Probe on IOwrite
  // Probe on IOread
  LED led_14 (.in(TS5));
  LED led_15 (.in(TS5noio));
  LED led_16 (.in(TS5io));
  LED led_17 (.in(TS5ior));
  LED led_18 (.in(TS5iow));
  PullDown pulldown_4 (.out(TS0));
  PullDown pulldown_5 (.out(TS1));
  and and_17 (TS3io, TS3, IOrw);
  and and_18 (TS4io, TS4, IOrw);
  and and_19 (TS5io, TS5, IOrw);
  and and_20 (TS6io, TS6, IOrw);
  and and_21 (TS7io, TS7, IOrw);
  not not_13 (not_13_out, TS3ior);
  LED led_19 (.in(TS6));
  LED led_20 (.in(TS6noio));
  LED led_21 (.in(TS6io));
  LED led_22 (.in(TS6ior));
  LED led_23 (.in(TS6iow));
  // _74LS283 _74ls283_5: pin names not known; wires that end beside it: _74ls283_4_p2, _74ls283_5_p2
  PullDown pulldown_6 (.out(TS2));
  PullDown pulldown_7 (.out(TS3));
  PullDown pulldown_8 (.out(TS4));
  PullDown pulldown_9 (.out(TS5));
  not not_14 (IOreadP, not_13_out);
  Delay #(.delayTime(20)) delay_3 (.in(TS4iow), .out(IOwriteP));
  or or_8 (IOrw, IOwrite, IOread);
  nor nor_9 (noIO, IOwrite, IOread);
  LED led_24 (.in(TS7));
  LED led_25 (.in(TS7noio));
  LED led_26 (.in(TS7io));
  LED led_27 (.in(TS7ior));
  LED led_28 (.in(TS7iow));
  PullDown pulldown_10 (.out(TS6));
  PullDown pulldown_11 (.out(TS7));
  // _74LS283 _74ls283_6: pin names not known; wires that end beside it: _74ls283_5_p2
  nand nand_4 (nand_4_out, SPY_sub[23], SPY_sub[23]);
  and and_22 (TS3noio, TS3, noIO);
  and and_23 (TS4noio, TS4, noIO);
  and and_24 (TS5noio, TS5, noIO);
  and and_25 (TS6noio, TS6, noIO);
  and and_26 (TS7noio, TS7, noIO);
  nand nand_5 (isLEQ, nand_4_out, nand_3_out);
  // _74LS245 _74ls245_1: pin names not known; wires that end beside it: 1'b1, nResult_E
  // _74LS245 _74ls245_2: pin names not known; wires that end beside it: 1'b1, nResult_E
  // _74LS245 _74ls245_3: pin names not known; wires that end beside it: 1'b1, nResult_E
  LED led_29 (.in(in_13));
  LED led_30 (.in(in_15));
  LED led_31 (.in(in_7));
  LED led_32 (.in(in_8));
  LED led_33 (.in(in_9));
  LED led_34 (.in(in_11));
  LED led_35 (.in(in_16));
  LED led_36 (.in(in_17));
  LED led_37 (.in(in_10));
  LED led_38 (.in(in_14));
  LED led_39 (.in(in_18));
  LED led_40 (.in(in_12));
  LED led_41 (.in(isLEQ));
  LED led_42 (.in(AisNeg));
  LED led_43 (.in(BisNeg));
  and and_27 (and_27_out, TS3, ~IOread);  // And
  or or_9 (or_9_out, TS0, TS2, TS5);
  or or_10 (or_10_out, TS0, TS1, TS2, and_27_out, TS5);
  or or_11 (or_11_out, TS1, TS3);
  or or_12 (or_12_out, TS1, TS3, TS4);
  or or_13 (or_13_out, TS1, TS3, TS6);
  and and_28 (and_28_out, TS4, nIOwrite);
  and and_29 (and_29_out, TS5, nIOwrite, isLEQ);
  PullDown pulldown_12 (.out(or_12_out));
  PullDown pulldown_13 (.out(or_13_out));
  PullDown pulldown_14 (.out(and_28_out));
  PullDown pulldown_15 (.out(TS4));
  PullDown pulldown_16 (.out(TS6));
  assign in_13 = or_9_out ? 1'b1 : 1'bz;  // Driver driver_1
  PullDown pulldown_17 (.out(or_9_out));
  assign in_15 = or_10_out ? 1'b1 : 1'bz;  // Driver driver_2
  PullDown pulldown_18 (.out(or_10_out));
  assign in_7 = or_11_out ? 1'b1 : 1'bz;  // Driver driver_3
  PullDown pulldown_19 (.out(or_11_out));
  assign in_8 = TS1 ? 1'b1 : 1'bz;  // Driver driver_4
  PullDown pulldown_20 (.out(TS1));
  assign in_9 = TS3 ? 1'b1 : 1'bz;  // Driver driver_5
  PullDown pulldown_21 (.out(TS3));
  assign in_11 = or_12_out ? 1'b1 : 1'bz;  // Driver driver_6
  assign in_16 = TS2 ? 1'b1 : 1'bz;  // Driver driver_7
  PullDown pulldown_22 (.out(TS2));
  assign in_17 = TS4 ? 1'b1 : 1'bz;  // Driver driver_8
  PullDown pulldown_23 (.out(TS4));
  assign in_10 = or_13_out ? 1'b1 : 1'bz;  // Driver driver_9
  assign in_14 = and_28_out ? 1'b1 : 1'bz;  // Driver driver_10
  assign in_18 = TS4 ? 1'b1 : 1'bz;  // Driver driver_11
  assign in_12 = and_29_out ? 1'b1 : 1'bz;  // Driver driver_12
  PullDown pulldown_24 (.out(and_29_out));
  assign in_19 = TS6 ? 1'b1 : 1'bz;  // Driver driver_13
  // _74LS175 _74ls175_1: pin names not known; wires that end beside it: in_8, 1'b1, SpyIOa[0], SpyIOa[1], SpyIOa[2], SpyIOa[3]
  // Probe on IOwriteP
  // Probe on IOreadP
  PullDown pulldown_25 (.out(in_7));
  PullDown pulldown_26 (.out(in_8));
  PullDown pulldown_27 (.out(in_9));
  PullDown pulldown_28 (.out(in_11));
  PullDown pulldown_29 (.out(in_10));
  PullDown pulldown_30 (.out(in_12));
  PullDown pulldown_31 (.out(in_13));
  PullDown pulldown_32 (.out(in_14));
  PullDown pulldown_33 (.out(in_15));
  PullDown pulldown_34 (.out(in_16));
  PullDown pulldown_35 (.out(in_17));
  PullDown pulldown_36 (.out(in_18));
  PullDown pulldown_37 (.out(in_19));
  PullDown pulldown_38 (.out(IOreadP));
  not not_15 (nMAR_E, in_11);
  not not_16 (nPC_LD, in_12);
  not not_17 (nE_PC, in_13);
  not not_18 (nWR, in_14);
  not not_19 (nRD, in_15);
  not not_20 (nResult_E, in_18);
  not not_21 (not_21_out, IOreadP);
  _74LS238 _74ls238_2 (
    .A(ABUS[0]), .B(ABUS[1]), .C(ABUS[2]), .G(IOwriteP), .nGA(1'b0), .nGB(1'b0), .Y0(_74ls238_2_y0),
    .Y1(_74ls238_2_y1), .Y2(_74ls238_2_y2), .Y3(_74ls238_2_y3), .Y4(_74ls238_2_y4), .Y5(_74ls238_2_y5),
    .Y6(_74ls238_2_y6), .Y7(_74ls238_2_y7));
  _74LS138 _74ls138_1 (
    .A(SpyIOa[0]), .B(SpyIOa[1]), .C(SpyIOa[2]), .G(IOreadP), .nGB(1'b0), .nGA(1'b0), .nY0(_74ls138_1_ny0),
    .nY1(_74ls138_1_ny1), .nY2(_74ls138_1_ny2), .nY3(_74ls138_1_ny3), .nY4(_74ls138_1_ny4),
    .nY5(_74ls138_1_ny5), .nY6(_74ls138_1_ny6), .nY7(_74ls138_1_ny7));
  // _74LS540 _74ls540_1: pin names not known; wires that end beside it: _74ls138_1_ny6, _74ls138_1_ny6
  _74LS541 _74ls541_1 (
    .nOE1(not_21_out), .nOE2(not_21_out), ._0D(1'b0), ._1D(1'b0), ._2D(1'b0), ._3D(1'b0), ._4D(1'b0),
    ._5D(1'b0), ._6D(1'b0), ._7D(1'b0), ._0O(DBUS[8]), ._1O(DBUS[9]), ._2O(DBUS[10]), ._3O(DBUS[11]),
    ._4O(DBUS[12]), ._5O(DBUS[13]), ._6O(DBUS[14]), ._7O(DBUS[15]));
  _74LS541 _74ls541_2 (
    .nOE1(not_21_out), .nOE2(not_21_out), ._0D(1'b0), ._1D(1'b0), ._2D(1'b0), ._3D(1'b0), ._4D(1'b0),
    ._5D(1'b0), ._6D(1'b0), ._7D(UARTdrives), ._0O(DBUS[16]), ._1O(DBUS[17]), ._2O(DBUS[18]), ._3O(DBUS[19]),
    ._4O(DBUS[20]), ._5O(DBUS[21]), ._6O(DBUS[22]), ._7O(DBUS[23]));
  // Probe on _74ls238_2_y0
  // Probe on _74ls238_2_y1
  // Probe on _74ls238_2_y2
  // Probe on _74ls238_2_y3
  // Probe on _74ls238_2_y4
  // Probe on _74ls238_2_y5
  // Probe on _74ls238_2_y6
  // Probe on _74ls238_2_y7
  // Probe on _74ls138_1_ny0
  // Probe on _74ls138_1_ny1
  // Probe on _74ls138_1_ny2
  // Probe on _74ls138_1_ny3
  // Probe on _74ls138_1_ny4
  // Probe on _74ls138_1_ny5
  // Probe on _74ls138_1_ny6
  // Probe on _74ls138_1_ny7
  // Probe on _74ls138_1_ny6
  not not_22 (not_22_out, _74ls138_1_ny0);
  not not_23 (not_23_out, _74ls138_1_ny7);
  PullDown pulldown_39 (.out(not_22_out));
  Half7474 half7474_18 (.nSD(1'b1), .D(not_30_out), .CP(clk), .nRD(1'b1), .Q(half7474_18_q));  // open: nQ
  Half7474 half7474_19 (.nSD(half7474_18_q), .D(1'b0), .CP(_74ls238_2_y7), .nRD(1'b1), .Q(half7474_19_q));  // open: nQ
  _74LS574 _74ls574_8 (
    .nOC(1'b0), .CLK(_74ls238_2_y7), .D0(DBUS[0]), .D1(DBUS[1]), .D2(DBUS[2]), .D3(DBUS[3]), .D4(DBUS[4]),
    .D5(DBUS[5]), .D6(DBUS[6]), .D7(DBUS[7]), .Q0(_74ls574_8_q0[0]), .Q1(_74ls574_8_q0[1]),
    .Q2(_74ls574_8_q0[2]), .Q3(_74ls574_8_q0[3]), .Q4(_74ls574_8_q0[4]), .Q5(_74ls574_8_q0[5]),
    .Q6(_74ls574_8_q0[6]), .Q7(_74ls574_8_q0[7]));  // open: SPY
  _74LS393 _74ls393_1 (
    ._1A(clk), ._1CL(not_25_out), ._2A(_74ls393_1__1qd), ._2CL(not_25_out), ._1QD(_74ls393_1__1qd),
    ._2QA(_74ls393_1__2qa), ._2QD(_74ls393_1__2qd));  // open: _1QA, _1QB, _1QC, _2QB, _2QC
  nand nand_6 (nand_6_out, half7474_22_q, not_23_out);
  not not_24 (not_24_out, in_19);
  nand nand_7 (nand_7_out, _74ls393_1__2qa, _74ls393_1__2qd);
  not not_25 (not_25_out, not_28_out);
  Half7474 half7474_20 (.nSD(nand_6_out), .D(1'b0), .CP(nResetP), .nRD(not_24_out), .Q(half7474_20_q));  // open: nQ
  nand nand_8 (UARTBusy, half7474_19_q, nUARTbusy);
  nand nand_9 (nUARTbusy, UARTBusy, nand_13_out);
  assign not_26_out = ~_74ls574_8_q0;  // Not not_26, 8 bits wide
  not not_27 (not_27_out, nand_7_out);
  not not_28 (not_28_out, half7474_21_nq);
  nand nand_10 (nand_10_out, half7474_20_q, in_19);
  // Probe on _74ls574_8_q0
  // Probe on not_26_out
  nand nand_11 (nand_11_out, _74ls393_1__1qd, not_27_out);
  // Probe on not_26_out
  nand nand_12 (nand_12_out, nUARTbusy, not_22_out);
  Delay #(.delayTime(10)) delay_4 (.in(nResetP), .out(delay_4_out));
  _74LS393 _74ls393_2 (
    ._1A(clk), ._1CL(nUARTbusy), ._2A(_74ls393_2__1qd), ._2CL(nUARTbusy), ._1QD(_74ls393_2__1qd),
    ._2QC(_74ls393_2__2qc), ._2QD(_74ls393_2__2qd));  // open: _1QA, _1QB, _1QC, _2QA, _2QB
  Half7474 half7474_21 (
    .nSD(uart_telnet_gw_1_tx), .D(1'b0), .CP(reset_2_out), .nRD(nand_11_out), .nQ(half7474_21_nq));  // open: Q
  Reset reset_2 (.out(reset_2_out));
  Half7474 half7474_22 (.nSD(nand_11_out), .D(1'b0), .CP(1'b0), .nRD(nand_10_out), .Q(half7474_22_q));  // open: nQ
  not not_29 (not_29_out, delay_4_out);
  Uart_Telnet_GW uart_telnet_gw_1 (.RX(_74ls165_2_nqh), .CLK(clk), .TX(uart_telnet_gw_1_tx));
  and and_30 (and_30_out, nPC_LD, nResetP);
  or or_14 (or_14_out, in_10, not_29_out);
  not not_30 (not_30_out, _74ls393_2__1qd);
  nand nand_13 (nand_13_out, _74ls393_2__2qc, _74ls393_2__2qd);
  not not_31 (not_31_out, uart_telnet_gw_1_tx);
  not not_32 (not_32_out, nand_6_out);
  _74LS157 _74ls157_1 (
    .S(nResetP), .A1(1'b0), .A2(1'b0), .A3(1'b0), .A4(1'b0), .B1(DBUS[0]), .B2(DBUS[1]), .B3(DBUS[2]),
    .B4(DBUS[3]), .G(1'b0), .Y1(_74ls157_1_y1), .Y2(_74ls157_1_y2), .Y3(_74ls157_1_y3), .Y4(_74ls157_1_y4));
  _74LS157 _74ls157_2 (
    .S(nResetP), .A1(1'b0), .A2(1'b0), .A3(1'b0), .A4(1'b0), .B1(DBUS[4]), .B2(DBUS[5]), .B3(DBUS[6]),
    .B4(DBUS[7]), .G(1'b0), .Y1(_74ls157_2_y1), .Y2(_74ls157_2_y2), .Y3(_74ls157_2_y3), .Y4(_74ls157_2_y4));
  _74LS157 _74ls157_3 (
    .S(nResetP), .A1(1'b0), .A2(1'b0), .A3(1'b0), .A4(1'b0), .B1(DBUS[8]), .B2(DBUS[9]), .B3(DBUS[10]),
    .B4(DBUS[11]), .G(1'b0), .Y1(_74ls157_3_y1), .Y2(_74ls157_3_y2), .Y3(_74ls157_3_y3), .Y4(_74ls157_3_y4));
  _74LS157 _74ls157_4 (
    .S(nResetP), .A1(1'b0), .A2(1'b0), .A3(1'b0), .A4(1'b0), .B1(DBUS[12]), .B2(DBUS[13]), .B3(DBUS[14]),
    .B4(DBUS[15]), .G(1'b0), .Y1(_74ls157_4_y1), .Y2(_74ls157_4_y2), .Y3(_74ls157_4_y3), .Y4(_74ls157_4_y4));
  _74LS157 _74ls157_5 (
    .S(nResetP), .A1(1'b0), .A2(1'b0), .A3(1'b0), .A4(1'b0), .B1(DBUS[16]), .B2(DBUS[17]), .B3(DBUS[18]),
    .B4(DBUS[19]), .G(1'b0), .Y1(_74ls157_5_y1), .Y2(_74ls157_5_y2), .Y3(_74ls157_5_y3), .Y4(_74ls157_5_y4));
  _74LS157 _74ls157_6 (
    .S(nResetP), .A1(1'b0), .A2(PC_FLASH), .A3(PC_FLASH), .A4(1'b0), .B1(DBUS[20]), .B2(DBUS[21]),
    .B3(DBUS[22]), .B4(DBUS[23]), .G(1'b0), .Y1(_74ls157_6_y1), .Y2(_74ls157_6_y2), .Y3(_74ls157_6_y3),
    .Y4(_74ls157_6_y4));
  _74LS165 _74ls165_1 (
    .nLD(half7474_19_q), .INH(1'b0), .CLK(not_30_out), .SER(1'b0), .A(1'b0), .B(1'b0), .C(1'b0), .D(1'b0),
    .E(1'b0), .F(1'b0), .G(1'b0), .H(_74ls574_8_q0[7]), .QH(_74ls165_1_qh));  // open: nQH
  // _74LS595 _74ls595_1: pin names not known; wires that end beside it: not_31_out, _74ls393_1__1qd, not_27_out, nand_6_out, 1'b1
  // Probe on DBUS[7:0]
  assign DBUS[15:8] = 1'b0 ? {8{1'b0}} : 8'bz;  // Driver driver_14
  assign DBUS[23:16] = 1'b0 ? {8{1'b0}} : 8'bz;  // Driver driver_15
  nand nand_14 (nand_14_out, not_32_out, not_23_out);
  and and_31 (UARTdrives, nand_14_out, nand_12_out);
  _74LS163 _74ls163_2 (
    .nPE(and_30_out), .nSR(1'b1), .CP(or_14_out), .CET(1'b1), .CEP(1'b1), .P0(_74ls157_1_y1),
    .P1(_74ls157_1_y2), .P2(_74ls157_1_y3), .P3(_74ls157_1_y4), .TC(_74ls163_2_tc), .Q0(SPY_PC[0]),
    .Q1(SPY_PC[1]), .Q2(SPY_PC[2]), .Q3(SPY_PC[3]));
  _74LS163 _74ls163_3 (
    .nPE(and_30_out), .nSR(1'b1), .CP(or_14_out), .CET(_74ls163_2_tc), .CEP(1'b1), .P0(_74ls157_2_y1),
    .P1(_74ls157_2_y2), .P2(_74ls157_2_y3), .P3(_74ls157_2_y4), .TC(_74ls163_3_tc), .Q0(SPY_PC[4]),
    .Q1(SPY_PC[5]), .Q2(SPY_PC[6]), .Q3(SPY_PC[7]));
  _74LS163 _74ls163_4 (
    .nPE(and_30_out), .nSR(1'b1), .CP(or_14_out), .CET(_74ls163_3_tc), .CEP(1'b1), .P0(_74ls157_3_y1),
    .P1(_74ls157_3_y2), .P2(_74ls157_3_y3), .P3(_74ls157_3_y4), .TC(_74ls163_4_tc), .Q0(SPY_PC[8]),
    .Q1(SPY_PC[9]), .Q2(SPY_PC[10]), .Q3(SPY_PC[11]));
  _74LS163 _74ls163_5 (
    .nPE(and_30_out), .nSR(1'b1), .CP(or_14_out), .CET(_74ls163_4_tc), .CEP(1'b1), .P0(_74ls157_4_y1),
    .P1(_74ls157_4_y2), .P2(_74ls157_4_y3), .P3(_74ls157_4_y4), .TC(_74ls163_5_tc), .Q0(SPY_PC[12]),
    .Q1(SPY_PC[13]), .Q2(SPY_PC[14]), .Q3(SPY_PC[15]));
  _74LS163 _74ls163_6 (
    .nPE(and_30_out), .nSR(1'b1), .CP(or_14_out), .CET(_74ls163_5_tc), .CEP(1'b1), .P0(_74ls157_5_y1),
    .P1(_74ls157_5_y2), .P2(_74ls157_5_y3), .P3(_74ls157_5_y4), .TC(_74ls163_6_tc), .Q0(SPY_PC[16]),
    .Q1(SPY_PC[17]), .Q2(SPY_PC[18]), .Q3(SPY_PC[19]));
  _74LS163 _74ls163_7 (
    .nPE(and_30_out), .nSR(1'b1), .CP(or_14_out), .CET(_74ls163_6_tc), .CEP(1'b1), .P0(_74ls157_6_y1),
    .P1(_74ls157_6_y2), .P2(_74ls157_6_y3), .P3(_74ls157_6_y4), .TC(_74ls163_7_tc), .Q0(SPY_PC[20]),
    .Q1(SPY_PC[21]), .Q2(SPY_PC[22]), .Q3(HALT_t));
  _74LS165 _74ls165_2 (
    .nLD(half7474_19_q), .INH(1'b0), .CLK(not_30_out), .SER(_74ls165_1_qh), .A(_74ls574_8_q0[6]),
    .B(_74ls574_8_q0[5]), .C(_74ls574_8_q0[4]), .D(_74ls574_8_q0[3]), .E(_74ls574_8_q0[2]),
    .F(_74ls574_8_q0[1]), .G(_74ls574_8_q0[0]), .H(1'b1), .nQH(_74ls165_2_nqh));  // open: QH
  // _74LS245 _74ls245_4: pin names not known; wires that end beside it: 1'b1, nE_PC
  // _74LS245 _74ls245_5: pin names not known; wires that end beside it: 1'b1, nE_PC
  // _74LS245 _74ls245_6: pin names not known; wires that end beside it: 1'b1, nE_PC
  LED END (.in(HALT_t));

  // Other names for the same wires on the sheet: A_CK = in_8; Aval_CK = in_16; B_CK = in_9; BAUD = clk;
  //   Bval_CK = in_17; CK = XTAL; E_PC = in_13; SPY_PC[23] = HALT_t; MAR_CK = in_7; MAR_E = in_11; MopEnd = in_19;
  //   PC_CK = in_10; PC_LD = in_12; RD = in_15; Result_E = in_18; WR = in_14

  // Notes on the sheet:
  //   clk: Hz: 4800
  //   XTAL: Hz: 50000
  //   GPIO2in: default 85
  //   RESET-F
  //   RESET-R
  //   microSTEP
  //   RUN/HALT
  //   STEP
  //   MAR & NEG
  //   CONTROL/SEQUENCER
  //   R W 
  //   0 0 = 1
  //   0 1 = 0 
  //   1 0 = 1
  //   1 1 = 1
  //   LATCHED SUBTRACTOR
  //   Carry In
  //   Out Enable
  //   MICROCODE
  //   DECODER
  //   PLAIN
  //   IO
  //   IO-read
  //   IO-write
  //   E_PC
  //   RD
  //   MAR_CK
  //   A_CK
  //   B_CK
  //   MAR_E
  //   Aval_CK
  //   Bval_CK
  //   PC_CK
  //   WR
  //   Res_E
  //   PC_LD
  //   LEQ
  //   A-
  //   B-
  //   if(a < 0) mem[b] += (int)getchar(); /* input */
  //           else if(b < 0) printf("%c", (char)mem[a]); /* output */
  //   stty -icanon -echo && nc localhost 23
  //   GPIO
  //   GPIOw
  //   AddrCk
  //   GPIOr
  //   UARTdrives
  //   UARTbusyRead
  //   UARTtrig
  //   UARTread
  //   UART
  //   SendCk
  //   ~D
  //   OE
  //   Status
  //   PROGRAM COUNTER
  //   ~Reset
  //   NewPC
  //   Flash
  //   ~OE
  //   ~LD
  //   CK
  //   ~Q
  //   Neg
  //   Q
endmodule
