// Digital circuit Subtractor.dig as structural Verilog
module Subtractor (
  input  [23:0] B,
  input  nOE,
  input  nCY,
  input  [23:0] A,
  output [23:0] Q,
  output LEQ
);

  wire _74ls283_1_p2, _74ls283_2_p2, _74ls283_3_p2, _74ls283_4_p2, _74ls283_5_p2, _74ls283_6_p2, nand_1_out,
       nand_2_out, nor_1_out, nor_2_out, nor_3_out, nor_4_out, nor_5_out, nor_6_out, nor_7_out, nor_8_out;
  wire [3:0] undriven, undriven_2, undriven_3, undriven_4, undriven_5, undriven_6;

  // _74LS283 _74ls283_1: pin names not known; wires that end beside it: nCY, _74ls283_1_p2
  // _74LS283 _74ls283_2: pin names not known; wires that end beside it: _74ls283_1_p2, _74ls283_2_p2
  nor nor_1 (nor_1_out, undriven[0], undriven[1], undriven[2]);
  nor nor_2 (nor_2_out, undriven[3], undriven_2[0], undriven_2[1]);
  nor nor_3 (nor_3_out, undriven_2[2], undriven_2[3], undriven_3[0]);
  nor nor_4 (nor_4_out, undriven_3[1], undriven_3[2], undriven_3[3]);
  nor nor_5 (nor_5_out, undriven_4[0], undriven_4[1], undriven_4[2]);
  nor nor_6 (nor_6_out, undriven_4[3], undriven_5[0], undriven_5[1]);
  nor nor_7 (nor_7_out, undriven_5[2], undriven_5[3], undriven_6[0]);
  nor nor_8 (nor_8_out, undriven_6[1], undriven_6[2], undriven_6[3]);
  // _74LS283 _74ls283_3: pin names not known; wires that end beside it: _74ls283_2_p2, _74ls283_3_p2
  nand nand_1 (nand_1_out, nor_1_out, nor_2_out, nor_3_out, nor_4_out, nor_5_out, nor_6_out, nor_7_out, nor_8_out);
  // _74LS283 _74ls283_4: pin names not known; wires that end beside it: _74ls283_3_p2, _74ls283_4_p2
  nand nand_2 (nand_2_out, undriven_6[3], undriven_6[3]);
  nand nand_3 (LEQ, nand_2_out, nand_1_out);
  // _74LS283 _74ls283_5: pin names not known; wires that end beside it: _74ls283_4_p2, _74ls283_5_p2
  // _74LS283 _74ls283_6: pin names not known; wires that end beside it: _74ls283_5_p2, _74ls283_6_p2, _74ls283_6_p2
  // _74LS245 _74ls245_1: pin names not known; wires that end beside it: 1'b1, nOE
  // _74LS245 _74ls245_2: pin names not known; wires that end beside it: 1'b1, nOE
  // _74LS245 _74ls245_3: pin names not known; wires that end beside it: 1'b1, nOE

  // Notes on the sheet:
  //   nOE: default 1
  //   nCY: default 1
endmodule
