// Digital circuit Uart_Telnet_GW.dig as structural Verilog
module Uart_Telnet_GW (
  input  RX,
  input  CLK,
  output TX
);

  wire _74ls393_1__1qd, _74ls393_1__2qa, _74ls393_1__2qd, _74ls393_2__1qd, _74ls393_2__2qa, _74ls393_2__2qd,
       _74165_1_p15, delay_1_out, delay_2_out, delay_3_out, delay_4_out, half7474_1_nq, half7474_2_q,
       nand_1_out, nand_2_out, nand_3_out, nand_4_out, nand_5_out, nand_6_out, not_1_out, not_2_out,
       not_3_out, not_4_out, not_5_out, not_6_out, or_1_out, or_2_out, reset_1_out, reset_2_out, telnet_1_av;
  wire [7:0] telnet_1_out, undriven;

  _74LS393 _74ls393_1 (
    ._1A(CLK), ._1CL(delay_1_out), ._2A(_74ls393_1__1qd), ._2CL(delay_1_out), ._1QD(_74ls393_1__1qd),
    ._2QA(_74ls393_1__2qa), ._2QD(_74ls393_1__2qd));  // open: _1QA, _1QB, _1QC, _2QB, _2QC
  nand nand_1 (nand_1_out, _74ls393_1__2qa, _74ls393_1__2qd);
  Delay #(.delayTime(2)) delay_1 (.in(half7474_1_nq), .out(delay_1_out));
  not not_1 (not_1_out, nand_1_out);
  not not_2 (not_2_out, delay_2_out);
  // Probe on half7474_1_nq
  Delay #(.delayTime(20)) delay_2 (.in(half7474_2_q), .out(delay_2_out));
  Delay #(.delayTime(10)) delay_3 (.in(or_1_out), .out(delay_3_out));
  or or_1 (or_1_out, delay_4_out, half7474_2_q);
  // Probe on half7474_2_q
  // Probe on _74ls393_1__1qd
  // Probe on not_1_out
  nand nand_2 (nand_2_out, _74ls393_1__1qd, not_1_out);
  Half7474 half7474_1 (.nSD(RX), .D(1'b0), .CP(reset_1_out), .nRD(nand_2_out), .nQ(half7474_1_nq));  // open: Q
  Reset reset_1 (.out(reset_1_out));
  // Probe on nand_2_out
  Half7474 half7474_2 (.nSD(nand_2_out), .D(1'b0), .CP(1'b0), .nRD(not_2_out), .Q(half7474_2_q));  // open: nQ
  PullDown pulldown_1 (.out(delay_3_out));
  PullDown pulldown_2 (.out(half7474_2_q));
  Telnet #(.telnetEscape("false")) telnet_1 (
    .in(undriven), .C(delay_3_out), .wr(half7474_2_q), .rd(telnet_1_av), .out(telnet_1_out), .av(telnet_1_av));
  PullDown pulldown_3 (.out(telnet_1_av));
  Delay #(.delayTime(5)) delay_4 (.in(telnet_1_av), .out(delay_4_out));
  // Probe on delay_4_out
  // _74595 _74595_1: pin names not known; wires that end beside it: RX, _74ls393_1__1qd, not_1_out, 1'b0, 1'b1, 1'b1, 1'b0
  // Probe on telnet_1_out
  or or_2 (or_2_out, delay_4_out, reset_2_out);
  Reset #(.invertOutput("false")) reset_2 (.out(reset_2_out));
  not not_3 (not_3_out, not_4_out);
  not not_4 (not_4_out, or_2_out);
  nand nand_3 (nand_3_out, not_5_out, or_2_out);
  not not_5 (not_5_out, not_3_out);
  // Probe on nand_3_out
  nand nand_4 (nand_4_out, nand_3_out, nand_5_out);
  nand nand_5 (nand_5_out, nand_4_out, nand_6_out);
  // Probe on nand_4_out
  // Probe on nand_5_out
  _74LS393 _74ls393_2 (
    ._1A(CLK), ._1CL(nand_5_out), ._2A(_74ls393_2__1qd), ._2CL(nand_5_out), ._1QD(_74ls393_2__1qd),
    ._2QA(_74ls393_2__2qa), ._2QD(_74ls393_2__2qd));  // open: _1QA, _1QB, _1QC, _2QB, _2QC
  not not_6 (not_6_out, _74ls393_2__1qd);
  nand nand_6 (nand_6_out, _74ls393_2__2qa, _74ls393_2__2qd);
  // Probe on not_6_out
  // _74165 _74165_1: pin names not known; wires that end beside it: nand_3_out, 1'b1, 1'b0, not_6_out, 1'b1, 1'b1, 1'b1, 1'b1, 1'b1, 1'b1, 1'b1, telnet_1_out[7], 1'b1, 1'b0, _74165_1_p15
  // _74165 _74165_2: pin names not known; wires that end beside it: nand_3_out, telnet_1_out[6], 1'b0, not_6_out, _74165_1_p15, telnet_1_out[5], telnet_1_out[4], telnet_1_out[3], telnet_1_out[2], telnet_1_out[1], telnet_1_out[0], 1'b0, 1'b1, 1'b0, TX
  // Probe on TX

  // Notes on the sheet:
  //   CLK: Hz: 1000
  //   SERIAL -> TELNET GATEWAY
  //   ONLY FOR TESTING IN SIMULATION
endmodule
